// Logisim project CSC3410-MicroArchitecture.circ as structural Verilog: 1 circuit, main circuit main
module main (
);

  // AND_Gate and_1 is placed but not wired

  // Notes on the sheet:
  //   Nick Zayatz
  //   Michele Burns
  //   Michael Newton
  //   Charlie Adams
  //   10/20/15
  //   Main File for CSC3410-MicroArchitecture Project
endmodule
